# Fritzing sketch PoolPumpController (saved by Fritzing 0.9.2b)
circuit board: 7.9007cm x 6.63776cm
breadboards: 1

parts:
  VR = Voltage Regulator - 5V [package="TO220 [THT]"]
  R1 = Resistor [tolerance=±5% resistance=4.7k package=THT]
  ATmega168 = atmega168 [package=dip]
  TTL = female pin header, 3 pins [form="♀ (female)"]
  U9 = mystery part, 10 pins [chip_label=?]
  U10 = mystery part, 10 pins [chip_label=?]
  C2 = Capacitor [part_number=470nF package=cap-pth-small2]
  Crystal = CRYSTAL [package=hc49u-v]
  C4 = Capacitor [part_number=22pF package=cap-pth-small2]
  C5 = Capacitor [part_number=22pF package=cap-pth-small2]
  Temp = female pin header, 3 pins [form="♀ (female)"]
  Q1 = NPN-Transistor [package="TO92 [THT]"]
  I2C = female pin header, 3 pins [form="♀ (female)"]
  R2 = Resistor [tolerance=±5% resistance=1k package=THT]
  R5 = Resistor [tolerance=±5% resistance=330 package=THT]
  D1 = Rectifier Diode [part_number=1N4001 package="300 mil [THT]"]
  C1 = Capacitor [package=cap-pth-5mm]
  GND = mystery part, 1 pin [chip_label=?]
  12V = mystery part, 1 pin [chip_label=?]
  SW1 = female pin header, 2 pins [form="♀ (female)"]
  R4 = Resistor [tolerance=±5% resistance=10k package=THT]
  LED = female pin header, 2 pins [form="♀ (female)"]
  R8 = Resistor [tolerance=±5% resistance=1k package=THT]
  R9 = Resistor [tolerance=±5% resistance=1k package=THT]
  AC_IN = mystery part, 1 pin [chip_label=?]  # not connected
  AC_IN_2 = mystery part, 1 pin [chip_label=?]  # not connected
  C3 = Electrolytic Capacitor [capacitance=47µF package="100 mil [THT, electrolytic]"]
  R3 = Resistor [tolerance=±5% resistance=10k package=THT]
  6V = mystery part, 1 pin [chip_label=?]
  GND_2 = mystery part, 1 pin [chip_label=?]

nets:
  N1: VR.input_voltage, C1.2, 12V.pin1, R8.Pin_1
  GND: VR.GND, ATmega168.GND, ATmega168.D6_(PWM), ATmega168.D7, ATmega168.D10_(PWM), ATmega168.D11_(PWM), ATmega168.D12, ATmega168.D13, ATmega168.A1, ATmega168.A2, ATmega168.A3, TTL.pin1, U9.pin10, C2.1, C4.2, C5.2, Temp.pin3, Q1.E, I2C.pin1, R5.Pin_0, C1.1, GND.pin1, R4.Pin_1, R9.Pin_0, C3.-, R3.Pin_0
  N2: VR.output_voltage, R1.Pin_1, ATmega168.VCC, ATmega168.AVCC, ATmega168.AREF, U9.pin1, C2.2, Temp.pin1, SW1.pin1, C3.+
  N3: R1.Pin_0, ATmega168.RESET
  N4: ATmega168.D0_(RX), TTL.pin3
  N5: ATmega168.D1_(TX), TTL.pin2
  N6: ATmega168.D2, R2.Pin_0
  N7: ATmega168.D3_(PWM), SW1.pin2, R4.Pin_0
  N8: ATmega168.D4, LED.pin1
  N9: ATmega168.XLAT1, Crystal.2, C4.1
  N10: ATmega168.XLAT2, Crystal.1, C5.1
  N11: ATmega168.D5_(PWM), U10.pin6
  N12: ATmega168.D8, U9.pin2
  N13: ATmega168.D9_(PWM), U9.pin3
  N14: ATmega168.A0, Temp.pin2
  N15: ATmega168.A4, I2C.pin3
  N16: ATmega168.A5, I2C.pin2
  N17: Q1.B, R2.Pin_1, R3.Pin_1
  N18: Q1.C, D1.anode, GND_2.pin1
  N19: R5.Pin_1, LED.pin2
  N20: D1.cathode, R8.Pin_0, R9.Pin_1, 6V.pin1

notes:
  Transformer
  120-240VAC IN
  Out to Coil
  GN
  Vo
  Vs
  SD
  SC
  XBee
  RX
  TX
  A0
  D2
  D4
  D9
  D8
  D5
  D3
  15
  10
  2
  1
  3
  D10
  DC OUT
